// Logisim project sumador_4_bits_solo_transistores.circ as structural Verilog: 11 circuits, main circuit Paso01_Transistor_N
module Paso01_Transistor_N (
  input  G,
  output Salida
);

  Transistor #(.\type ("n")) transistor_1 (.in(1'b0), .out(Salida), .gate(G));

  // Notes on the sheet:
  //   LECCIÓN 1: el transistor N (NMOS) es un INTERRUPTOR que se cierra con 1
  //   Tiene 3 patas:  G = compuerta (la "palanca")   D = drenaje   S = fuente.  La corriente pasa entre D y S sólo si G lo permite.
  //   G
  //   D
  //   S
  //   tierra = GND = − = 0
  //   PRUEBA con la manito (Ctrl+1): haz clic en G.
  //   G = 1  ->  el interruptor se CIERRA: la Salida queda unida a tierra  ->  Salida = 0
  //   G = 0  ->  el interruptor se ABRE: la Salida no toca nada  ->  queda "flotando"
  //                 (Logisim lo muestra AZUL y con una U: no vale ni 0 ni 1, está desconectada)
  //   Regla para acordarte:  N = se activa con 1  y sirve para bajar la salida a 0 (a tierra).
  //    G | interruptor | Salida
  //    0 |  abierto    | flotando
  //    1 |  cerrado    |    0
endmodule

module Paso02_Transistor_P (
  input  G,
  output Salida
);

  Transistor #(.\type ("p")) transistor_1 (.in(1'b1), .out(Salida), .gate(G));

  // Notes on the sheet:
  //   LECCIÓN 2: el transistor P (PMOS) es el "opuesto": un interruptor que se cierra con 0
  //   Fíjate en la BOLITA que tiene en la pata G: en electrónica una bolita significa "al revés" (se activa con 0).
  //   G
  //   + = VDD = voltaje = 1
  //   S
  //   D
  //   PRUEBA con la manito: haz clic en G.
  //   G = 0  ->  el interruptor se CIERRA: la Salida queda unida al +  ->  Salida = 1
  //   G = 1  ->  el interruptor se ABRE: la Salida queda flotando (azul)
  //   Regla para acordarte:  P = se activa con 0  y sirve para subir la salida a 1 (al +).
  //   Por eso en TODAS las compuertas los P van ARRIBA (pegados al +) y los N ABAJO (pegados a tierra).
  //    G | interruptor | Salida
  //    0 |  cerrado    |    1
  //    1 |  abierto    | flotando
endmodule

module Paso03_NOT (
  input  A,
  output Y
);

  Transistor #(.\type ("p")) transistor_1 (.in(1'b1), .out(Y), .gate(A));
  Transistor #(.\type ("n")) transistor_2 (.in(1'b0), .out(Y), .gate(A));
  LED led_1 (.in(Y));

  // Notes on the sheet:
  //   NOT (inversor) con 2 transistores
  //   1 PMOS arriba y 1 NMOS abajo. Si A=1 el NMOS une Y con GND (Y=0); si A=0 el PMOS une Y con VDD (Y=1).
  //   Todo está hecho SOLO con transistores: arriba PMOS (conducen con 0), abajo NMOS (conducen con 1).
  //    A | Y
  //    0 | 1
  //    1 | 0
endmodule

module Paso04_NAND (
  input  A,
  input  B,
  output Y
);

  wire transistor_3_out;

  Transistor #(.\type ("p")) transistor_1 (.in(1'b1), .out(Y), .gate(A));
  Transistor #(.\type ("n")) transistor_2 (.in(transistor_3_out), .out(Y), .gate(A));
  Transistor #(.\type ("n")) transistor_3 (.in(1'b0), .out(transistor_3_out), .gate(B));
  Transistor #(.\type ("p")) transistor_4 (.in(1'b1), .out(Y), .gate(B));
  LED led_1 (.in(Y));

  // Notes on the sheet:
  //   NAND con 4 transistores
  //   2 PMOS en paralelo arriba y 2 NMOS en serie abajo: sólo si A=1 y B=1 la salida baja a 0.
  //   Todo está hecho SOLO con transistores: arriba PMOS (conducen con 0), abajo NMOS (conducen con 1).
  //    A  B | Y
  //    0  0 | 1
  //    0  1 | 1
  //    1  0 | 1
  //    1  1 | 0
endmodule

module Paso05_NOR (
  input  A,
  input  B,
  output Y
);

  wire transistor_1_out;

  Transistor #(.\type ("p")) transistor_1 (.in(1'b1), .out(transistor_1_out), .gate(B));
  Transistor #(.\type ("p")) transistor_2 (.in(transistor_1_out), .out(Y), .gate(A));
  Transistor #(.\type ("n")) transistor_3 (.in(1'b0), .out(Y), .gate(B));
  Transistor #(.\type ("n")) transistor_4 (.in(1'b0), .out(Y), .gate(A));
  LED led_1 (.in(Y));

  // Notes on the sheet:
  //   NOR con 4 transistores
  //   Al revés que la NAND: 2 PMOS en SERIE arriba y 2 NMOS en PARALELO abajo. Sólo si A=0 y B=0 sale 1.
  //   Todo está hecho SOLO con transistores: arriba PMOS (conducen con 0), abajo NMOS (conducen con 1).
  //    A  B | Y
  //    0  0 | 1
  //    0  1 | 0
  //    1  0 | 0
  //    1  1 | 0
endmodule

module Paso06_AND (
  input  A,
  input  B,
  output Y
);

  wire transistor_1_out, transistor_3_out;

  Transistor #(.\type ("p")) transistor_1 (.in(1'b1), .out(transistor_1_out), .gate(A));
  Transistor #(.\type ("n")) transistor_2 (.in(transistor_3_out), .out(transistor_1_out), .gate(A));
  Transistor #(.\type ("n")) transistor_3 (.in(1'b0), .out(transistor_3_out), .gate(B));
  Transistor #(.\type ("p")) transistor_4 (.in(1'b1), .out(transistor_1_out), .gate(B));
  Transistor #(.\type ("p")) transistor_5 (.in(1'b1), .out(Y), .gate(transistor_1_out));
  Transistor #(.\type ("n")) transistor_6 (.in(1'b0), .out(Y), .gate(transistor_1_out));
  LED led_1 (.in(Y));

  // Notes on the sheet:
  //   AND con 6 transistores  (NAND + inversor)
  //   Los 4 de la izquierda hacen NAND; los 2 de la derecha la invierten y queda AND.
  //   Todo está hecho SOLO con transistores: arriba PMOS (conducen con 0), abajo NMOS (conducen con 1).
  //    A  B | Y
  //    0  0 | 0
  //    0  1 | 0
  //    1  0 | 0
  //    1  1 | 1
endmodule

module Paso07_OR (
  input  A,
  input  B,
  output Y
);

  wire transistor_1_out, transistor_2_out;

  Transistor #(.\type ("p")) transistor_1 (.in(1'b1), .out(transistor_1_out), .gate(B));
  Transistor #(.\type ("p")) transistor_2 (.in(transistor_1_out), .out(transistor_2_out), .gate(A));
  Transistor #(.\type ("n")) transistor_3 (.in(1'b0), .out(transistor_2_out), .gate(B));
  Transistor #(.\type ("n")) transistor_4 (.in(1'b0), .out(transistor_2_out), .gate(A));
  Transistor #(.\type ("p")) transistor_5 (.in(1'b1), .out(Y), .gate(transistor_2_out));
  Transistor #(.\type ("n")) transistor_6 (.in(1'b0), .out(Y), .gate(transistor_2_out));
  LED led_1 (.in(Y));

  // Notes on the sheet:
  //   OR con 6 transistores  (NOR + inversor)
  //   Los 4 de la izquierda hacen NOR; los 2 de la derecha la invierten y queda OR.
  //   Todo está hecho SOLO con transistores: arriba PMOS (conducen con 0), abajo NMOS (conducen con 1).
  //    A  B | Y
  //    0  0 | 0
  //    0  1 | 1
  //    1  0 | 1
  //    1  1 | 1
endmodule

module Paso08_XOR (
  input  A,
  input  B,
  output Y
);

  wire transistor_1_out, transistor_3_out, transistor_5_out, transistor_6_out, transistor_9_out,
       transistor_12_out, transistor_15_out;

  Transistor #(.\type ("p")) transistor_1 (.in(1'b1), .out(transistor_1_out), .gate(A));
  Transistor #(.\type ("n")) transistor_2 (.in(transistor_3_out), .out(transistor_1_out), .gate(A));
  Transistor #(.\type ("n")) transistor_3 (.in(1'b0), .out(transistor_3_out), .gate(B));
  Transistor #(.\type ("p")) transistor_4 (.in(1'b1), .out(transistor_1_out), .gate(B));
  Transistor #(.\type ("p")) transistor_5 (.in(1'b1), .out(transistor_5_out), .gate(A));
  Transistor #(.\type ("p")) transistor_6 (.in(1'b1), .out(transistor_6_out), .gate(transistor_1_out));
  Transistor #(.\type ("p")) transistor_7 (.in(1'b1), .out(transistor_5_out), .gate(transistor_1_out));
  Transistor #(.\type ("n")) transistor_8 (.in(transistor_9_out), .out(transistor_5_out), .gate(A));
  Transistor #(.\type ("n")) transistor_9 (.in(1'b0), .out(transistor_9_out), .gate(transistor_1_out));
  Transistor #(.\type ("p")) transistor_10 (.in(1'b1), .out(transistor_6_out), .gate(B));
  Transistor #(.\type ("n")) transistor_11 (.in(transistor_12_out), .out(transistor_6_out), .gate(transistor_1_out));
  Transistor #(.\type ("n")) transistor_12 (.in(1'b0), .out(transistor_12_out), .gate(B));
  Transistor #(.\type ("p")) transistor_13 (.in(1'b1), .out(Y), .gate(transistor_5_out));
  Transistor #(.\type ("n")) transistor_14 (.in(transistor_15_out), .out(Y), .gate(transistor_5_out));
  Transistor #(.\type ("n")) transistor_15 (.in(1'b0), .out(transistor_15_out), .gate(transistor_6_out));
  Transistor #(.\type ("p")) transistor_16 (.in(1'b1), .out(Y), .gate(transistor_6_out));
  LED led_1 (.in(Y));

  // Notes on the sheet:
  //   XOR con 16 transistores
  //   4 grupos NAND (4 transistores cada uno). Da 1 sólo cuando A y B son distintos.
  //   Todo está hecho SOLO con transistores: arriba PMOS (conducen con 0), abajo NMOS (conducen con 1).
  //    A  B | Y
  //    0  0 | 0
  //    0  1 | 1
  //    1  0 | 1
  //    1  1 | 0
endmodule

module Paso09_Medio_sumador (
  input  A,
  input  B,
  output S,
  output C
);

  wire transistor_1_out, transistor_3_out, transistor_5_out, transistor_6_out, transistor_9_out,
       transistor_12_out, transistor_15_out;

  Transistor #(.\type ("p")) transistor_1 (.in(1'b1), .out(transistor_1_out), .gate(A));
  Transistor #(.\type ("n")) transistor_2 (.in(transistor_3_out), .out(transistor_1_out), .gate(A));
  Transistor #(.\type ("n")) transistor_3 (.in(1'b0), .out(transistor_3_out), .gate(B));
  Transistor #(.\type ("p")) transistor_4 (.in(1'b1), .out(transistor_1_out), .gate(B));
  Transistor #(.\type ("p")) transistor_5 (.in(1'b1), .out(transistor_5_out), .gate(A));
  Transistor #(.\type ("p")) transistor_6 (.in(1'b1), .out(transistor_6_out), .gate(transistor_1_out));
  Transistor #(.\type ("p")) transistor_7 (.in(1'b1), .out(transistor_5_out), .gate(transistor_1_out));
  Transistor #(.\type ("n")) transistor_8 (.in(transistor_9_out), .out(transistor_5_out), .gate(A));
  Transistor #(.\type ("n")) transistor_9 (.in(1'b0), .out(transistor_9_out), .gate(transistor_1_out));
  Transistor #(.\type ("p")) transistor_10 (.in(1'b1), .out(transistor_6_out), .gate(B));
  Transistor #(.\type ("n")) transistor_11 (.in(transistor_12_out), .out(transistor_6_out), .gate(transistor_1_out));
  Transistor #(.\type ("n")) transistor_12 (.in(1'b0), .out(transistor_12_out), .gate(B));
  Transistor #(.\type ("p")) transistor_13 (.in(1'b1), .out(S), .gate(transistor_5_out));
  Transistor #(.\type ("n")) transistor_14 (.in(transistor_15_out), .out(S), .gate(transistor_5_out));
  Transistor #(.\type ("n")) transistor_15 (.in(1'b0), .out(transistor_15_out), .gate(transistor_6_out));
  Transistor #(.\type ("p")) transistor_16 (.in(1'b1), .out(C), .gate(transistor_1_out));
  Transistor #(.\type ("n")) transistor_17 (.in(1'b0), .out(C), .gate(transistor_1_out));
  Transistor #(.\type ("p")) transistor_18 (.in(1'b1), .out(S), .gate(transistor_6_out));
  LED led_1 (.in(S));
  LED led_2 (.in(C));

  // Notes on the sheet:
  //   Medio sumador con 18 transistores
  //   S = A XOR B (los 16 de arriba)   C = acarreo = NOT de la primera NAND (2 transistores más).
  //   Todo está hecho SOLO con transistores: arriba PMOS (conducen con 0), abajo NMOS (conducen con 1).
  //    A + B = C S
  //    0 + 0 = 0 0
  //    0 + 1 = 0 1
  //    1 + 0 = 0 1
  //    1 + 1 = 1 0
endmodule

module Paso10_Sumador_completo (
  input  Cin,
  input  A,
  input  B,
  output S,
  output Cout
);

  wire transistor_1_out, transistor_3_out, transistor_5_out, transistor_6_out, transistor_9_out,
       transistor_12_out, transistor_13_out, transistor_15_out, transistor_17_out, transistor_20_out,
       transistor_21_out, transistor_23_out, transistor_24_out, transistor_26_out, transistor_33_out,
       transistor_36_out;

  Transistor #(.\type ("p")) transistor_1 (.in(1'b1), .out(transistor_1_out), .gate(A));
  Transistor #(.\type ("n")) transistor_2 (.in(transistor_3_out), .out(transistor_1_out), .gate(A));
  Transistor #(.\type ("n")) transistor_3 (.in(1'b0), .out(transistor_3_out), .gate(B));
  Transistor #(.\type ("p")) transistor_4 (.in(1'b1), .out(transistor_1_out), .gate(B));
  Transistor #(.\type ("p")) transistor_5 (.in(1'b1), .out(transistor_5_out), .gate(A));
  Transistor #(.\type ("p")) transistor_6 (.in(1'b1), .out(transistor_6_out), .gate(transistor_1_out));
  Transistor #(.\type ("p")) transistor_7 (.in(1'b1), .out(transistor_5_out), .gate(transistor_1_out));
  Transistor #(.\type ("n")) transistor_8 (.in(transistor_9_out), .out(transistor_5_out), .gate(A));
  Transistor #(.\type ("n")) transistor_9 (.in(1'b0), .out(transistor_9_out), .gate(transistor_1_out));
  Transistor #(.\type ("p")) transistor_10 (.in(1'b1), .out(transistor_6_out), .gate(B));
  Transistor #(.\type ("n")) transistor_11 (.in(transistor_12_out), .out(transistor_6_out), .gate(transistor_1_out));
  Transistor #(.\type ("n")) transistor_12 (.in(1'b0), .out(transistor_12_out), .gate(B));
  Transistor #(.\type ("p")) transistor_13 (.in(1'b1), .out(transistor_13_out), .gate(transistor_5_out));
  Transistor #(.\type ("n")) transistor_14 (.in(transistor_15_out), .out(transistor_13_out), .gate(transistor_5_out));
  Transistor #(.\type ("n")) transistor_15 (.in(1'b0), .out(transistor_15_out), .gate(transistor_6_out));
  Transistor #(.\type ("p")) transistor_16 (.in(1'b1), .out(transistor_13_out), .gate(transistor_6_out));
  Transistor #(.\type ("p")) transistor_17 (.in(1'b1), .out(transistor_17_out), .gate(transistor_13_out));
  Transistor #(.\type ("p")) transistor_18 (.in(1'b1), .out(transistor_17_out), .gate(Cin));
  Transistor #(.\type ("n")) transistor_19 (.in(transistor_20_out), .out(transistor_17_out), .gate(transistor_13_out));
  Transistor #(.\type ("n")) transistor_20 (.in(1'b0), .out(transistor_20_out), .gate(Cin));
  Transistor #(.\type ("p")) transistor_21 (.in(1'b1), .out(transistor_21_out), .gate(transistor_13_out));
  Transistor #(.\type ("n")) transistor_22 (.in(transistor_23_out), .out(transistor_21_out), .gate(transistor_13_out));
  Transistor #(.\type ("n")) transistor_23 (.in(1'b0), .out(transistor_23_out), .gate(transistor_17_out));
  Transistor #(.\type ("p")) transistor_24 (.in(1'b1), .out(transistor_24_out), .gate(Cin));
  Transistor #(.\type ("n")) transistor_25 (.in(transistor_26_out), .out(transistor_24_out), .gate(Cin));
  Transistor #(.\type ("n")) transistor_26 (.in(1'b0), .out(transistor_26_out), .gate(transistor_17_out));
  Transistor #(.\type ("p")) transistor_27 (.in(1'b1), .out(transistor_21_out), .gate(transistor_17_out));
  Transistor #(.\type ("p")) transistor_28 (.in(1'b1), .out(transistor_24_out), .gate(transistor_17_out));
  Transistor #(.\type ("p")) transistor_29 (.in(1'b1), .out(S), .gate(transistor_21_out));
  Transistor #(.\type ("p")) transistor_30 (.in(1'b1), .out(Cout), .gate(transistor_1_out));
  Transistor #(.\type ("p")) transistor_31 (.in(1'b1), .out(S), .gate(transistor_24_out));
  Transistor #(.\type ("n")) transistor_32 (.in(transistor_33_out), .out(S), .gate(transistor_21_out));
  Transistor #(.\type ("n")) transistor_33 (.in(1'b0), .out(transistor_33_out), .gate(transistor_24_out));
  Transistor #(.\type ("p")) transistor_34 (.in(1'b1), .out(Cout), .gate(transistor_17_out));
  Transistor #(.\type ("n")) transistor_35 (.in(transistor_36_out), .out(Cout), .gate(transistor_1_out));
  Transistor #(.\type ("n")) transistor_36 (.in(1'b0), .out(transistor_36_out), .gate(transistor_17_out));
  LED led_1 (.in(S));
  LED led_2 (.in(Cout));

  // Notes on the sheet:
  //   Sumador completo con 36 transistores
  //   9 grupos NAND de 4 transistores. Suma A + B + Cin (el acarreo que viene de la columna anterior).
  //   Todo está hecho SOLO con transistores: arriba PMOS (conducen con 0), abajo NMOS (conducen con 1).
  //    A B Cin | Cout S
  //    0 0  0  |  0   0
  //    0 0  1  |  0   1
  //    0 1  0  |  0   1
  //    0 1  1  |  1   0
  //    1 0  0  |  0   1
  //    1 0  1  |  1   0
  //    1 1  0  |  1   0
  //    1 1  1  |  1   1
endmodule

module Paso11_Sumador_4_bits (
  input  A0,
  input  B0,
  input  A1,
  input  B1,
  input  A2,
  input  B2,
  input  A3,
  input  B3,
  output S0,
  output S1,
  output S2,
  output S3,
  output S4,
  output [4:0] Suma
);

  wire transistor_1_out, transistor_3_out, transistor_4_out, transistor_6_out, transistor_7_out,
       transistor_9_out, transistor_10_out, transistor_12_out, transistor_17_out, transistor_18_out,
       transistor_19_out, transistor_20_out, transistor_21_out, transistor_22_out, transistor_23_out,
       transistor_24_out, transistor_27_out, transistor_30_out, transistor_33_out, transistor_36_out,
       transistor_39_out, transistor_42_out, transistor_45_out, transistor_48_out, transistor_49_out,
       transistor_51_out, transistor_52_out, transistor_54_out, transistor_55_out, transistor_57_out,
       transistor_58_out, transistor_60_out, transistor_65_out, transistor_66_out, transistor_67_out,
       transistor_68_out, transistor_71_out, transistor_74_out, transistor_77_out, transistor_80_out,
       transistor_81_out, transistor_83_out, transistor_84_out, transistor_86_out, transistor_87_out,
       transistor_89_out, transistor_90_out, transistor_92_out, transistor_93_out, transistor_95_out,
       transistor_96_out, transistor_98_out, transistor_99_out, transistor_101_out, transistor_102_out,
       transistor_104_out, transistor_114_out, transistor_116_out, transistor_118_out, transistor_123_out,
       transistor_126_out, transistor_129_out, transistor_132_out, transistor_135_out, transistor_138_out,
       transistor_141_out, transistor_144_out;

  Transistor #(.\type ("p")) transistor_1 (.in(1'b1), .out(transistor_1_out), .gate(A0));
  Transistor #(.\type ("n")) transistor_2 (.in(transistor_3_out), .out(transistor_1_out), .gate(A0));
  Transistor #(.\type ("n")) transistor_3 (.in(1'b0), .out(transistor_3_out), .gate(B0));
  Transistor #(.\type ("p")) transistor_4 (.in(1'b1), .out(transistor_4_out), .gate(A1));
  Transistor #(.\type ("n")) transistor_5 (.in(transistor_6_out), .out(transistor_4_out), .gate(A1));
  Transistor #(.\type ("n")) transistor_6 (.in(1'b0), .out(transistor_6_out), .gate(B1));
  Transistor #(.\type ("p")) transistor_7 (.in(1'b1), .out(transistor_7_out), .gate(A2));
  Transistor #(.\type ("n")) transistor_8 (.in(transistor_9_out), .out(transistor_7_out), .gate(A2));
  Transistor #(.\type ("n")) transistor_9 (.in(1'b0), .out(transistor_9_out), .gate(B2));
  Transistor #(.\type ("p")) transistor_10 (.in(1'b1), .out(transistor_10_out), .gate(A3));
  Transistor #(.\type ("n")) transistor_11 (.in(transistor_12_out), .out(transistor_10_out), .gate(A3));
  Transistor #(.\type ("n")) transistor_12 (.in(1'b0), .out(transistor_12_out), .gate(B3));
  Transistor #(.\type ("p")) transistor_13 (.in(1'b1), .out(transistor_1_out), .gate(B0));
  Transistor #(.\type ("p")) transistor_14 (.in(1'b1), .out(transistor_4_out), .gate(B1));
  Transistor #(.\type ("p")) transistor_15 (.in(1'b1), .out(transistor_7_out), .gate(B2));
  Transistor #(.\type ("p")) transistor_16 (.in(1'b1), .out(transistor_10_out), .gate(B3));
  Transistor #(.\type ("p")) transistor_17 (.in(1'b1), .out(transistor_17_out), .gate(A0));
  Transistor #(.\type ("p")) transistor_18 (.in(1'b1), .out(transistor_18_out), .gate(transistor_1_out));
  Transistor #(.\type ("p")) transistor_19 (.in(1'b1), .out(transistor_19_out), .gate(A1));
  Transistor #(.\type ("p")) transistor_20 (.in(1'b1), .out(transistor_20_out), .gate(transistor_4_out));
  Transistor #(.\type ("p")) transistor_21 (.in(1'b1), .out(transistor_21_out), .gate(A2));
  Transistor #(.\type ("p")) transistor_22 (.in(1'b1), .out(transistor_22_out), .gate(transistor_7_out));
  Transistor #(.\type ("p")) transistor_23 (.in(1'b1), .out(transistor_23_out), .gate(A3));
  Transistor #(.\type ("p")) transistor_24 (.in(1'b1), .out(transistor_24_out), .gate(transistor_10_out));
  Transistor #(.\type ("p")) transistor_25 (.in(1'b1), .out(transistor_17_out), .gate(transistor_1_out));
  Transistor #(.\type ("n")) transistor_26 (.in(transistor_27_out), .out(transistor_17_out), .gate(A0));
  Transistor #(.\type ("n")) transistor_27 (.in(1'b0), .out(transistor_27_out), .gate(transistor_1_out));
  Transistor #(.\type ("p")) transistor_28 (.in(1'b1), .out(transistor_18_out), .gate(B0));
  Transistor #(.\type ("n")) transistor_29 (.in(transistor_30_out), .out(transistor_18_out), .gate(transistor_1_out));
  Transistor #(.\type ("n")) transistor_30 (.in(1'b0), .out(transistor_30_out), .gate(B0));
  Transistor #(.\type ("p")) transistor_31 (.in(1'b1), .out(transistor_19_out), .gate(transistor_4_out));
  Transistor #(.\type ("n")) transistor_32 (.in(transistor_33_out), .out(transistor_19_out), .gate(A1));
  Transistor #(.\type ("n")) transistor_33 (.in(1'b0), .out(transistor_33_out), .gate(transistor_4_out));
  Transistor #(.\type ("p")) transistor_34 (.in(1'b1), .out(transistor_20_out), .gate(B1));
  Transistor #(.\type ("n")) transistor_35 (.in(transistor_36_out), .out(transistor_20_out), .gate(transistor_4_out));
  Transistor #(.\type ("n")) transistor_36 (.in(1'b0), .out(transistor_36_out), .gate(B1));
  Transistor #(.\type ("p")) transistor_37 (.in(1'b1), .out(transistor_21_out), .gate(transistor_7_out));
  Transistor #(.\type ("n")) transistor_38 (.in(transistor_39_out), .out(transistor_21_out), .gate(A2));
  Transistor #(.\type ("n")) transistor_39 (.in(1'b0), .out(transistor_39_out), .gate(transistor_7_out));
  Transistor #(.\type ("p")) transistor_40 (.in(1'b1), .out(transistor_22_out), .gate(B2));
  Transistor #(.\type ("n")) transistor_41 (.in(transistor_42_out), .out(transistor_22_out), .gate(transistor_7_out));
  Transistor #(.\type ("n")) transistor_42 (.in(1'b0), .out(transistor_42_out), .gate(B2));
  Transistor #(.\type ("p")) transistor_43 (.in(1'b1), .out(transistor_23_out), .gate(transistor_10_out));
  Transistor #(.\type ("n")) transistor_44 (.in(transistor_45_out), .out(transistor_23_out), .gate(A3));
  Transistor #(.\type ("n")) transistor_45 (.in(1'b0), .out(transistor_45_out), .gate(transistor_10_out));
  Transistor #(.\type ("p")) transistor_46 (.in(1'b1), .out(transistor_24_out), .gate(B3));
  Transistor #(.\type ("n")) transistor_47 (.in(transistor_48_out), .out(transistor_24_out), .gate(transistor_10_out));
  Transistor #(.\type ("n")) transistor_48 (.in(1'b0), .out(transistor_48_out), .gate(B3));
  Transistor #(.\type ("p")) transistor_49 (.in(1'b1), .out(transistor_49_out), .gate(transistor_17_out));
  Transistor #(.\type ("n")) transistor_50 (.in(transistor_51_out), .out(transistor_49_out), .gate(transistor_17_out));
  Transistor #(.\type ("n")) transistor_51 (.in(1'b0), .out(transistor_51_out), .gate(transistor_18_out));
  Transistor #(.\type ("p")) transistor_52 (.in(1'b1), .out(transistor_52_out), .gate(transistor_19_out));
  Transistor #(.\type ("n")) transistor_53 (.in(transistor_54_out), .out(transistor_52_out), .gate(transistor_19_out));
  Transistor #(.\type ("n")) transistor_54 (.in(1'b0), .out(transistor_54_out), .gate(transistor_20_out));
  Transistor #(.\type ("p")) transistor_55 (.in(1'b1), .out(transistor_55_out), .gate(transistor_21_out));
  Transistor #(.\type ("n")) transistor_56 (.in(transistor_57_out), .out(transistor_55_out), .gate(transistor_21_out));
  Transistor #(.\type ("n")) transistor_57 (.in(1'b0), .out(transistor_57_out), .gate(transistor_22_out));
  Transistor #(.\type ("p")) transistor_58 (.in(1'b1), .out(transistor_58_out), .gate(transistor_23_out));
  Transistor #(.\type ("n")) transistor_59 (.in(transistor_60_out), .out(transistor_58_out), .gate(transistor_23_out));
  Transistor #(.\type ("n")) transistor_60 (.in(1'b0), .out(transistor_60_out), .gate(transistor_24_out));
  Transistor #(.\type ("p")) transistor_61 (.in(1'b1), .out(transistor_49_out), .gate(transistor_18_out));
  Transistor #(.\type ("p")) transistor_62 (.in(1'b1), .out(transistor_52_out), .gate(transistor_20_out));
  Transistor #(.\type ("p")) transistor_63 (.in(1'b1), .out(transistor_55_out), .gate(transistor_22_out));
  Transistor #(.\type ("p")) transistor_64 (.in(1'b1), .out(transistor_58_out), .gate(transistor_24_out));
  Transistor #(.\type ("p")) transistor_65 (.in(1'b1), .out(transistor_65_out), .gate(transistor_49_out));
  Transistor #(.\type ("p")) transistor_66 (.in(1'b1), .out(transistor_66_out), .gate(transistor_52_out));
  Transistor #(.\type ("p")) transistor_67 (.in(1'b1), .out(transistor_67_out), .gate(transistor_55_out));
  Transistor #(.\type ("p")) transistor_68 (.in(1'b1), .out(transistor_68_out), .gate(transistor_58_out));
  Transistor #(.\type ("p")) transistor_69 (.in(1'b1), .out(transistor_65_out), .gate(1'b0));
  Transistor #(.\type ("n")) transistor_70 (.in(transistor_71_out), .out(transistor_65_out), .gate(transistor_49_out));
  Transistor #(.\type ("n")) transistor_71 (.in(1'b0), .out(transistor_71_out), .gate(1'b0));
  Transistor #(.\type ("p")) transistor_72 (.in(1'b1), .out(transistor_66_out), .gate(transistor_114_out));
  Transistor #(.\type ("n")) transistor_73 (.in(transistor_74_out), .out(transistor_66_out), .gate(transistor_52_out));
  Transistor #(.\type ("n")) transistor_74 (.in(1'b0), .out(transistor_74_out), .gate(transistor_114_out));
  Transistor #(.\type ("p")) transistor_75 (.in(1'b1), .out(transistor_67_out), .gate(transistor_116_out));
  Transistor #(.\type ("n")) transistor_76 (.in(transistor_77_out), .out(transistor_67_out), .gate(transistor_55_out));
  Transistor #(.\type ("n")) transistor_77 (.in(1'b0), .out(transistor_77_out), .gate(transistor_116_out));
  Transistor #(.\type ("p")) transistor_78 (.in(1'b1), .out(transistor_68_out), .gate(transistor_118_out));
  Transistor #(.\type ("n")) transistor_79 (.in(transistor_80_out), .out(transistor_68_out), .gate(transistor_58_out));
  Transistor #(.\type ("n")) transistor_80 (.in(1'b0), .out(transistor_80_out), .gate(transistor_118_out));
  Transistor #(.\type ("p")) transistor_81 (.in(1'b1), .out(transistor_81_out), .gate(transistor_49_out));
  Transistor #(.\type ("n")) transistor_82 (.in(transistor_83_out), .out(transistor_81_out), .gate(transistor_49_out));
  Transistor #(.\type ("n")) transistor_83 (.in(1'b0), .out(transistor_83_out), .gate(transistor_65_out));
  Transistor #(.\type ("p")) transistor_84 (.in(1'b1), .out(transistor_84_out), .gate(1'b0));
  Transistor #(.\type ("n")) transistor_85 (.in(transistor_86_out), .out(transistor_84_out), .gate(1'b0));
  Transistor #(.\type ("n")) transistor_86 (.in(1'b0), .out(transistor_86_out), .gate(transistor_65_out));
  Transistor #(.\type ("p")) transistor_87 (.in(1'b1), .out(transistor_87_out), .gate(transistor_52_out));
  Transistor #(.\type ("n")) transistor_88 (.in(transistor_89_out), .out(transistor_87_out), .gate(transistor_52_out));
  Transistor #(.\type ("n")) transistor_89 (.in(1'b0), .out(transistor_89_out), .gate(transistor_66_out));
  Transistor #(.\type ("p")) transistor_90 (.in(1'b1), .out(transistor_90_out), .gate(transistor_114_out));
  Transistor #(.\type ("n")) transistor_91 (.in(transistor_92_out), .out(transistor_90_out), .gate(transistor_114_out));
  Transistor #(.\type ("n")) transistor_92 (.in(1'b0), .out(transistor_92_out), .gate(transistor_66_out));
  Transistor #(.\type ("p")) transistor_93 (.in(1'b1), .out(transistor_93_out), .gate(transistor_55_out));
  Transistor #(.\type ("n")) transistor_94 (.in(transistor_95_out), .out(transistor_93_out), .gate(transistor_55_out));
  Transistor #(.\type ("n")) transistor_95 (.in(1'b0), .out(transistor_95_out), .gate(transistor_67_out));
  Transistor #(.\type ("p")) transistor_96 (.in(1'b1), .out(transistor_96_out), .gate(transistor_116_out));
  Transistor #(.\type ("n")) transistor_97 (.in(transistor_98_out), .out(transistor_96_out), .gate(transistor_116_out));
  Transistor #(.\type ("n")) transistor_98 (.in(1'b0), .out(transistor_98_out), .gate(transistor_67_out));
  Transistor #(.\type ("p")) transistor_99 (.in(1'b1), .out(transistor_99_out), .gate(transistor_58_out));
  Transistor #(.\type ("n")) transistor_100 (
    .in(transistor_101_out), .out(transistor_99_out), .gate(transistor_58_out));
  Transistor #(.\type ("n")) transistor_101 (.in(1'b0), .out(transistor_101_out), .gate(transistor_68_out));
  Transistor #(.\type ("p")) transistor_102 (.in(1'b1), .out(transistor_102_out), .gate(transistor_118_out));
  Transistor #(.\type ("n")) transistor_103 (
    .in(transistor_104_out), .out(transistor_102_out), .gate(transistor_118_out));
  Transistor #(.\type ("n")) transistor_104 (.in(1'b0), .out(transistor_104_out), .gate(transistor_68_out));
  Transistor #(.\type ("p")) transistor_105 (.in(1'b1), .out(transistor_81_out), .gate(transistor_65_out));
  Transistor #(.\type ("p")) transistor_106 (.in(1'b1), .out(transistor_84_out), .gate(transistor_65_out));
  Transistor #(.\type ("p")) transistor_107 (.in(1'b1), .out(transistor_87_out), .gate(transistor_66_out));
  Transistor #(.\type ("p")) transistor_108 (.in(1'b1), .out(transistor_90_out), .gate(transistor_66_out));
  Transistor #(.\type ("p")) transistor_109 (.in(1'b1), .out(transistor_93_out), .gate(transistor_67_out));
  Transistor #(.\type ("p")) transistor_110 (.in(1'b1), .out(transistor_96_out), .gate(transistor_67_out));
  Transistor #(.\type ("p")) transistor_111 (.in(1'b1), .out(transistor_99_out), .gate(transistor_68_out));
  Transistor #(.\type ("p")) transistor_112 (.in(1'b1), .out(transistor_102_out), .gate(transistor_68_out));
  Transistor #(.\type ("p")) transistor_113 (.in(1'b1), .out(S0), .gate(transistor_81_out));
  Transistor #(.\type ("p")) transistor_114 (.in(1'b1), .out(transistor_114_out), .gate(transistor_1_out));
  Transistor #(.\type ("p")) transistor_115 (.in(1'b1), .out(S1), .gate(transistor_87_out));
  Transistor #(.\type ("p")) transistor_116 (.in(1'b1), .out(transistor_116_out), .gate(transistor_4_out));
  Transistor #(.\type ("p")) transistor_117 (.in(1'b1), .out(S2), .gate(transistor_93_out));
  Transistor #(.\type ("p")) transistor_118 (.in(1'b1), .out(transistor_118_out), .gate(transistor_7_out));
  Transistor #(.\type ("p")) transistor_119 (.in(1'b1), .out(S3), .gate(transistor_99_out));
  Transistor #(.\type ("p")) transistor_120 (.in(1'b1), .out(S4), .gate(transistor_10_out));
  Transistor #(.\type ("p")) transistor_121 (.in(1'b1), .out(S0), .gate(transistor_84_out));
  Transistor #(.\type ("n")) transistor_122 (.in(transistor_123_out), .out(S0), .gate(transistor_81_out));
  Transistor #(.\type ("n")) transistor_123 (.in(1'b0), .out(transistor_123_out), .gate(transistor_84_out));
  Transistor #(.\type ("p")) transistor_124 (.in(1'b1), .out(transistor_114_out), .gate(transistor_65_out));
  Transistor #(.\type ("n")) transistor_125 (
    .in(transistor_126_out), .out(transistor_114_out), .gate(transistor_1_out));
  Transistor #(.\type ("n")) transistor_126 (.in(1'b0), .out(transistor_126_out), .gate(transistor_65_out));
  Transistor #(.\type ("p")) transistor_127 (.in(1'b1), .out(S1), .gate(transistor_90_out));
  Transistor #(.\type ("n")) transistor_128 (.in(transistor_129_out), .out(S1), .gate(transistor_87_out));
  Transistor #(.\type ("n")) transistor_129 (.in(1'b0), .out(transistor_129_out), .gate(transistor_90_out));
  Transistor #(.\type ("p")) transistor_130 (.in(1'b1), .out(transistor_116_out), .gate(transistor_66_out));
  Transistor #(.\type ("n")) transistor_131 (
    .in(transistor_132_out), .out(transistor_116_out), .gate(transistor_4_out));
  Transistor #(.\type ("n")) transistor_132 (.in(1'b0), .out(transistor_132_out), .gate(transistor_66_out));
  Transistor #(.\type ("p")) transistor_133 (.in(1'b1), .out(S2), .gate(transistor_96_out));
  Transistor #(.\type ("n")) transistor_134 (.in(transistor_135_out), .out(S2), .gate(transistor_93_out));
  Transistor #(.\type ("n")) transistor_135 (.in(1'b0), .out(transistor_135_out), .gate(transistor_96_out));
  Transistor #(.\type ("p")) transistor_136 (.in(1'b1), .out(transistor_118_out), .gate(transistor_67_out));
  Transistor #(.\type ("n")) transistor_137 (
    .in(transistor_138_out), .out(transistor_118_out), .gate(transistor_7_out));
  Transistor #(.\type ("n")) transistor_138 (.in(1'b0), .out(transistor_138_out), .gate(transistor_67_out));
  Transistor #(.\type ("p")) transistor_139 (.in(1'b1), .out(S3), .gate(transistor_102_out));
  Transistor #(.\type ("n")) transistor_140 (.in(transistor_141_out), .out(S3), .gate(transistor_99_out));
  Transistor #(.\type ("n")) transistor_141 (.in(1'b0), .out(transistor_141_out), .gate(transistor_102_out));
  Transistor #(.\type ("p")) transistor_142 (.in(1'b1), .out(S4), .gate(transistor_68_out));
  Transistor #(.\type ("n")) transistor_143 (.in(transistor_144_out), .out(S4), .gate(transistor_10_out));
  Transistor #(.\type ("n")) transistor_144 (.in(1'b0), .out(transistor_144_out), .gate(transistor_68_out));
  LED led_1 (.in(S0));
  LED led_2 (.in(S1));
  LED led_3 (.in(S2));
  LED led_4 (.in(S3));
  LED led_5 (.in(S4));

  assign Suma = {S4, S3, S2, S1, S0};

  // Notes on the sheet:
  //   Cin = 0 (tierra)
  //   BIT 0  (vale 1)
  //   BIT 1  (vale 2)
  //   BIT 2  (vale 4)
  //   BIT 3  (vale 8)
  //   Sumador de 4 bits hecho SOLO con transistores (144 transistores)
  //   Cada bit es un sumador completo de 36 transistores. Con la MANITO cambia A0..A3 y B0..B3 (a la izquierda).
  //   El resultado sale a la derecha: S0..S3 en LEDs rojos, S4 (acarreo final) en naranjo, y el número en decimal abajo.
  //   Ejemplo: A = 0101 (5) y B = 0011 (3)  ->  Suma = 8.   Usa el botón "Auto" para ver todo el circuito.
  //   acarreo al bit siguiente
  //   acarreo al bit siguiente
  //   acarreo al bit siguiente
  //   resultado en decimal
endmodule
